// Logisim project Alperturk_2315752_ALL_CIRCUITS.circ as structural Verilog
module manipulate8bitnum (
  input  [7:0] In1,
  output O1,
  output [7:0] O2
);

  not not_1 (O2[7], In1[7]);
  and and_1 (O1, In1[0], In1[7]);

  assign O2[6:0] = In1[6:0];
endmodule

module rotr (
  input  [7:0] A,
  input  [2:0] B,
  output [7:0] O1
);

  Multiplexer #(.select(3), .width(8)) multiplexer_1 (
    .in0(A), .in1({A[0], A[7:1]}), .in2({A[1:0], A[7:2]}), .in3({A[2:0], A[7:3]}), .in4({A[3:0], A[7:4]}),
    .in5({A[4:0], A[7:5]}), .in6({A[5:0], A[7:6]}), .in7({A[6:0], A[7]}), .out(O1), .sel(B));
endmodule

module rotl (
  input  [7:0] A,
  input  [2:0] B,
  output [7:0] O1
);

  Multiplexer #(.select(3), .width(8)) multiplexer_1 (
    .in0(A), .in1({A[6:0], A[7]}), .in2({A[5:0], A[7:6]}), .in3({A[4:0], A[7:5]}), .in4({A[3:0], A[7:4]}),
    .in5({A[2:0], A[7:3]}), .in6({A[1:0], A[7:2]}), .in7({A[0], A[7:1]}), .out(O1), .sel(B));
endmodule

module FADDER1bit (
  input  A,
  input  B,
  input  Carry_In,
  output Result,
  output Carry_Out
);

  wire and_1_out, and_2_out, xor_1_out;

  xor xor_1 (xor_1_out, A, B);
  xor xor_2 (Result, xor_1_out, Carry_In);
  and and_1 (and_1_out, xor_1_out, Carry_In);
  and and_2 (and_2_out, A, B);
  or or_1 (Carry_Out, and_1_out, and_2_out);
endmodule

module FADDER4bit (
  input  CIN,
  input  [3:0] X,
  input  [3:0] Y,
  output [3:0] SUM,
  output COUT
);

  wire Cout1, Cout2, Cout3;

  FADDER1bit fadder1bit_1 (.A(CIN), .B(Y[0]), .Carry_In(X[0]), .Result(SUM[0]), .Carry_Out(Cout1));
  FADDER1bit fadder1bit_2 (.A(Cout1), .B(X[1]), .Carry_In(Y[1]), .Result(SUM[1]), .Carry_Out(Cout2));
  FADDER1bit fadder1bit_3 (.A(Cout2), .B(X[2]), .Carry_In(Y[2]), .Result(SUM[2]), .Carry_Out(Cout3));
  FADDER1bit fadder1bit_4 (.A(Cout3), .B(X[3]), .Carry_In(Y[3]), .Result(SUM[3]), .Carry_Out(COUT));
endmodule

module Alperturk_2315752_ALU8 (
  input  [7:0] X,
  input  [7:0] Y,
  input  [1:0] Opcode,
  output OVF,
  output CF,
  output SF,
  output ZF,
  output [7:0] RESULT,
  output EQ
);

  wire [7:0] alperturk_2315752_fadder8_1_sum, and_1_out, or_1_out, rotl_1_o1;
  wire [15:0] demultiplexer_1_out0, demultiplexer_1_out1, demultiplexer_1_out2, demultiplexer_1_out3;

  Demultiplexer #(.select(2), .tristate("true"), .width(16)) demultiplexer_1 (
    .out0(demultiplexer_1_out0), .out1(demultiplexer_1_out1), .out2(demultiplexer_1_out2),
    .out3(demultiplexer_1_out3), .in({Y, X}), .sel(Opcode));
  EQ_check eq_check_1 (.X(X), .Y(Y), .EQ(EQ));
  assign and_1_out = demultiplexer_1_out1[7:0] & demultiplexer_1_out1[15:8];  // AND_Gate and_1, 8 bits wide
  assign or_1_out = demultiplexer_1_out2[7:0] | demultiplexer_1_out2[15:8];  // OR_Gate or_1, 8 bits wide
  Alperturk_2315752_FADDER8 alperturk_2315752_fadder8_1 (
    .CIN(1'b0), .X(demultiplexer_1_out0[7:0]), .Y(demultiplexer_1_out0[15:8]),
    .SUM(alperturk_2315752_fadder8_1_sum), .COUT(CF));
  rotl rotl_1 (.A(demultiplexer_1_out3[7:0]), .B(demultiplexer_1_out3[10:8]), .O1(rotl_1_o1));
  Multiplexer #(.select(2), .width(8)) multiplexer_1 (
    .in0(alperturk_2315752_fadder8_1_sum), .in1(and_1_out), .in2(or_1_out), .in3(rotl_1_o1), .out(RESULT),
    .sel(Opcode));
  OVF_check ovf_check_1 (
    .RESULT(alperturk_2315752_fadder8_1_sum), .Y(demultiplexer_1_out0[7:0]), .X(demultiplexer_1_out0[15:8]),
    .OVF(OVF));
  SF_check sf_check_1 (.RESULT(alperturk_2315752_fadder8_1_sum), .SF(SF));
  EQ_check eq_check_2 (.X({8{1'b0}}), .Y(RESULT), .EQ(ZF));
endmodule

module Alperturk_2315752_FADDER8 (
  input  CIN,
  input  [7:0] X,
  input  [7:0] Y,
  output [7:0] SUM,
  output COUT
);

  wire Cout1;

  FADDER4bit fadder4bit_1 (.CIN(CIN), .X(X[3:0]), .Y(Y[3:0]), .SUM(SUM[3:0]), .COUT(Cout1));
  FADDER4bit fadder4bit_2 (.CIN(Cout1), .X(X[7:4]), .Y(Y[7:4]), .SUM(SUM[7:4]), .COUT(COUT));

  // Other names for the same wires on the sheet: Input2[3:0] = Y[3:0]
endmodule

module EQ_check (
  input  [7:0] X,
  input  [7:0] Y,
  output EQ
);

  wire xnor_1_out, xnor_2_out, xnor_3_out, xnor_4_out, xnor_5_out, xnor_6_out, xnor_7_out, xnor_8_out;

  xnor xnor_1 (xnor_1_out, X[0], Y[0]);
  xnor xnor_2 (xnor_2_out, X[1], Y[1]);
  xnor xnor_3 (xnor_3_out, X[2], Y[2]);
  xnor xnor_4 (xnor_4_out, X[3], Y[3]);
  xnor xnor_5 (xnor_5_out, X[4], Y[4]);
  xnor xnor_6 (xnor_6_out, X[5], Y[5]);
  xnor xnor_7 (xnor_7_out, X[6], Y[6]);
  xnor xnor_8 (xnor_8_out, X[7], Y[7]);
  and and_1 (EQ, xnor_1_out, xnor_2_out, xnor_3_out, xnor_4_out, xnor_5_out, xnor_6_out, xnor_7_out, xnor_8_out);
endmodule

module SF_check (
  input  [7:0] RESULT,
  output SF
);

  and and_1 (SF, 1'b1, RESULT[7]);
endmodule

module OVF_check (
  input  [7:0] RESULT,
  input  [7:0] Y,
  input  [7:0] X,
  output OVF
);

  wire and_1_out, and_2_out, not_1_out, not_2_out, not_3_out;

  not not_1 (not_1_out, Y[7]);
  not not_2 (not_2_out, X[7]);
  not not_3 (not_3_out, RESULT[7]);
  and and_1 (and_1_out, RESULT[7], not_1_out, not_2_out);
  and and_2 (and_2_out, not_3_out, Y[7], X[7]);
  or or_1 (OVF, and_1_out, and_2_out);
endmodule
