// Logisim project oguzhan_2315752.circ as structural Verilog: 7 circuits, main circuit ALU8
// ALU
module ALU8 (
  input  [7:0] X,
  input  [7:0] Y,
  input  [1:0] ALUfunc,
  output [7:0] RESULT
);

  wire [7:0] adder_1_out, and_1_out, or_1_out, shifter_1_out;

  Adder adder_1 (.a(X), .b(Y), .out(adder_1_out));  // open: cin, cout
  Shifter #(.shift("rl")) shifter_1 (.in(X), .\dist (Y[2:0]), .out(shifter_1_out));
  assign and_1_out = X & Y;  // AND_Gate and_1, 8 bits wide
  assign or_1_out = X | Y;  // OR_Gate or_1, 8 bits wide
  Multiplexer #(.select(2), .width(8)) multiplexer_1 (
    .in0(adder_1_out), .in1(and_1_out), .in2(or_1_out), .in3(shifter_1_out), .out(RESULT), .sel(ALUfunc));
endmodule

module REG_FILE (
  input  WE,
  input  [2:0] RD,
  input  [7:0] Write_data,
  input  Clk,
  input  [2:0] RS,
  input  [2:0] RT,
  output [7:0] Read_data1,
  output [7:0] Read_data2
);

  wire decoder_1_out0, decoder_1_out1, decoder_1_out2, decoder_1_out3, decoder_1_out4, decoder_1_out5,
       decoder_1_out6, decoder_1_out7;
  wire [7:0] register_1_q, register_2_q, register_3_q, register_4_q, register_5_q, register_6_q,
       register_7_q, register_8_q;

  Decoder #(.select(3)) decoder_1 (
    .out0(decoder_1_out0), .out1(decoder_1_out1), .out2(decoder_1_out2), .out3(decoder_1_out3),
    .out4(decoder_1_out4), .out5(decoder_1_out5), .out6(decoder_1_out6), .out7(decoder_1_out7), .sel(RD),
    .en(WE));
  Register #(.trigger("falling")) register_1 (
    .D(Write_data), .en(decoder_1_out0), .clk(Clk), .Q(register_1_q));  // open: clr
  Multiplexer #(.select(3), .width(8)) multiplexer_1 (
    .in0(register_1_q), .in1(register_2_q), .in2(register_3_q), .in3(register_4_q), .in4(register_5_q),
    .in5(register_6_q), .in6(register_7_q), .in7(register_8_q), .out(Read_data1), .sel(RS));
  Multiplexer #(.select(3), .width(8)) multiplexer_2 (
    .in0(register_1_q), .in1(register_2_q), .in2(register_3_q), .in3(register_4_q), .in4(register_5_q),
    .in5(register_6_q), .in6(register_7_q), .in7(register_8_q), .out(Read_data2), .sel(RT));
  Register #(.trigger("falling")) register_2 (
    .D(Write_data), .en(decoder_1_out1), .clk(Clk), .Q(register_2_q));  // open: clr
  Register #(.trigger("falling")) register_3 (
    .D(Write_data), .en(decoder_1_out2), .clk(Clk), .Q(register_3_q));  // open: clr
  Register #(.trigger("falling")) register_4 (
    .D(Write_data), .en(decoder_1_out3), .clk(Clk), .Q(register_4_q));  // open: clr
  Register #(.trigger("falling")) register_5 (
    .D(Write_data), .en(decoder_1_out4), .clk(Clk), .Q(register_5_q));  // open: clr
  Register #(.trigger("falling")) register_6 (
    .D(Write_data), .en(decoder_1_out5), .clk(Clk), .Q(register_6_q));  // open: clr
  Register #(.trigger("falling")) register_7 (
    .D(Write_data), .en(decoder_1_out6), .clk(Clk), .Q(register_7_q));  // open: clr
  Register #(.trigger("falling")) register_8 (
    .D(Write_data), .en(decoder_1_out7), .clk(Clk), .Q(register_8_q));  // open: clr
endmodule

module Instruction_Memory (
  input  [9:0] Address,
  output [3:0] OPCODE,
  output [2:0] RS,
  output [2:0] RT,
  output [2:0] RD,
  output [7:0] Immediate
);

  ROM #(.addrWidth(10), .dataWidth(21), .misaligned("true")) rom_1 (
    .addr(Address), .data({OPCODE, RS, RT, RD, Immediate}));

  // Notes on the sheet:
  //   contents of rom_1 (hex, n*v repeats v):
  //   60108 60204 88b00 8c00 188d00 44300 67
endmodule

module Data_Memory (
  input  [7:0] Address,
  input  WRITE,
  input  READ,
  input  Clk,
  input  [7:0] Write_data,
  output [7:0] Read_data
);

  RAM #(.asyncread("true"), .trigger("falling")) ram_1 (
    .addr(Address), .we(WRITE), .oe(READ), .clk(Clk), .din(Write_data), .dout(Read_data));
endmodule

module CPU (
);

  wire Clk, control_1_mux2, control_1_mw, control_1_we, control_1_wr;
  wire [1:0] control_1_alufunc, control_1_mux1;
  wire [2:0] instruction_memory_1_rd, instruction_memory_1_rs, instruction_memory_1_rt;
  wire [3:0] instruction_memory_1_opcode;
  wire [7:0] alu8_1_result, data_memory_1_read_data, instruction_memory_1_immediate, multiplexer_1_out,
       multiplexer_2_out, reg_file_1_read_data1, reg_file_1_read_data2;
  wire [9:0] adder_1_out, pc_1_addr_out;

  Clock clock_1 (.out(Clk));
  Adder #(.width(10)) adder_1 (.a(10'h1), .b(pc_1_addr_out), .out(adder_1_out));  // open: cin, cout
  PC pc_1 (.addr_in(adder_1_out), .in_2(Clk), .addr_out(pc_1_addr_out));
  Instruction_Memory instruction_memory_1 (
    .Address(pc_1_addr_out), .OPCODE(instruction_memory_1_opcode), .RS(instruction_memory_1_rs),
    .RT(instruction_memory_1_rt), .RD(instruction_memory_1_rd), .Immediate(instruction_memory_1_immediate));
  CONTROL control_1 (
    .in_1(instruction_memory_1_opcode), .Mux1(control_1_mux1), .Mux2(control_1_mux2), .WE(control_1_we),
    .MW(control_1_mw), .WR(control_1_wr), .ALUfunc(control_1_alufunc));
  Multiplexer #(.select(2), .width(8)) multiplexer_1 (
    .in0(alu8_1_result), .in1(data_memory_1_read_data), .in2(instruction_memory_1_immediate),
    .out(multiplexer_1_out), .sel(control_1_mux1));  // open: in3
  REG_FILE reg_file_1 (
    .WE(control_1_we), .RD(instruction_memory_1_rd), .Write_data(multiplexer_1_out), .Clk(Clk),
    .RS(instruction_memory_1_rs), .RT(instruction_memory_1_rt), .Read_data1(reg_file_1_read_data1),
    .Read_data2(reg_file_1_read_data2));
  Multiplexer #(.width(8)) multiplexer_2 (
    .in0(reg_file_1_read_data2), .in1(instruction_memory_1_immediate), .out(multiplexer_2_out),
    .sel(control_1_mux2));
  ALU8 alu8_1 (.X(reg_file_1_read_data1), .Y(multiplexer_2_out), .ALUfunc(control_1_alufunc), .RESULT(alu8_1_result));
  Data_Memory data_memory_1 (
    .Address(alu8_1_result), .WRITE(control_1_mw), .READ(control_1_wr), .Clk(Clk),
    .Write_data(reg_file_1_read_data2), .Read_data(data_memory_1_read_data));
endmodule

module PC (
  input  [9:0] addr_in,
  input  in_2,
  output [9:0] addr_out
);

  Register #(.trigger("falling"), .width(10)) register_1 (.D(addr_in), .clk(in_2), .Q(addr_out));  // open: en, clr
endmodule

module CONTROL (
  input  [3:0] in_1,
  output [1:0] Mux1,
  output Mux2,
  output WE,
  output MW,
  output WR,
  output [1:0] ALUfunc
);

  wire not_1_out, not_2_out, not_3_out, not_4_out;

  not not_1 (not_1_out, in_1[1]);
  not not_2 (not_2_out, in_1[1]);
  not not_3 (not_3_out, in_1[0]);
  not not_4 (not_4_out, in_1[1]);
  or or_1 (Mux2, in_1[0], in_1[1]);
  or or_2 (WE, in_1[0], not_2_out);
  and and_1 (MW, not_3_out, in_1[1]);
  and and_2 (WR, in_1[0], not_4_out);
  and and_3 (Mux1[1], in_1[0], in_1[1]);
  and and_4 (Mux1[0], in_1[0], not_1_out);

  assign ALUfunc = in_1[3:2];
endmodule
