// Logisim project oguzhan_2315752.circ as structural Verilog: 7 circuits, main circuit ALU8
// ALU
module ALU8 (
  input  [7:0] X,
  input  [7:0] Y,
  input  [2:0] ALUfunc,
  output EQ,
  output [7:0] RESULT
);

  wire comparator_1_lt;
  wire [7:0] adder_1_out, and_1_out, bit_extender_1_out, or_1_out, shifter_1_out;

  Comparator comparator_1 (.a(X), .b(Y), .eq(EQ), .lt(comparator_1_lt));  // open: gt
  Adder adder_1 (.a(X), .b(Y), .out(adder_1_out));  // open: cin, cout
  Shifter #(.shift("rl")) shifter_1 (.in(X), .\dist (Y[2:0]), .out(shifter_1_out));
  assign and_1_out = X & Y;  // AND_Gate and_1, 8 bits wide
  assign or_1_out = X | Y;  // OR_Gate or_1, 8 bits wide
  assign bit_extender_1_out = {{7{comparator_1_lt}}, comparator_1_lt};  // Bit_Extender bit_extender_1
  Multiplexer #(.select(3), .width(8)) multiplexer_1 (
    .in0(adder_1_out), .in1(and_1_out), .in2(or_1_out), .in3(shifter_1_out), .in4(bit_extender_1_out),
    .out(RESULT), .sel(ALUfunc));  // open: in5, in6, in7
endmodule

module REG_FILE (
  input  WE,
  input  [2:0] RD,
  input  [7:0] Write_data,
  input  Clk,
  input  [2:0] RS,
  input  [2:0] RT,
  output [7:0] Read_data1,
  output [7:0] Read_data2
);

  wire decoder_1_out0, decoder_1_out1, decoder_1_out2, decoder_1_out3, decoder_1_out4, decoder_1_out5,
       decoder_1_out6, decoder_1_out7;
  wire [7:0] register_1_q, register_2_q, register_3_q, register_4_q, register_5_q, register_6_q,
       register_7_q, register_8_q;

  Decoder #(.select(3)) decoder_1 (
    .out0(decoder_1_out0), .out1(decoder_1_out1), .out2(decoder_1_out2), .out3(decoder_1_out3),
    .out4(decoder_1_out4), .out5(decoder_1_out5), .out6(decoder_1_out6), .out7(decoder_1_out7), .sel(RD),
    .en(WE));
  Register #(.trigger("falling")) register_1 (
    .D(Write_data), .en(decoder_1_out0), .clk(Clk), .Q(register_1_q));  // open: clr
  Multiplexer #(.select(3), .width(8)) multiplexer_1 (
    .in0(register_1_q), .in1(register_2_q), .in2(register_3_q), .in3(register_4_q), .in4(register_5_q),
    .in5(register_6_q), .in6(register_7_q), .in7(register_8_q), .out(Read_data1), .sel(RS));
  Multiplexer #(.select(3), .width(8)) multiplexer_2 (
    .in0(register_1_q), .in1(register_2_q), .in2(register_3_q), .in3(register_4_q), .in4(register_5_q),
    .in5(register_6_q), .in6(register_7_q), .in7(register_8_q), .out(Read_data2), .sel(RT));
  Register #(.trigger("falling")) register_2 (
    .D(Write_data), .en(decoder_1_out1), .clk(Clk), .Q(register_2_q));  // open: clr
  Register #(.trigger("falling")) register_3 (
    .D(Write_data), .en(decoder_1_out2), .clk(Clk), .Q(register_3_q));  // open: clr
  Register #(.trigger("falling")) register_4 (
    .D(Write_data), .en(decoder_1_out3), .clk(Clk), .Q(register_4_q));  // open: clr
  Register #(.trigger("falling")) register_5 (
    .D(Write_data), .en(decoder_1_out4), .clk(Clk), .Q(register_5_q));  // open: clr
  Register #(.trigger("falling")) register_6 (
    .D(Write_data), .en(decoder_1_out5), .clk(Clk), .Q(register_6_q));  // open: clr
  Register #(.trigger("falling")) register_7 (
    .D(Write_data), .en(decoder_1_out6), .clk(Clk), .Q(register_7_q));  // open: clr
  Register #(.trigger("falling")) register_8 (
    .D(Write_data), .en(decoder_1_out7), .clk(Clk), .Q(register_8_q));  // open: clr
endmodule

module Instruction_Memory (
  input  [9:0] Address,
  output [9:0] JUMP,
  output [3:0] OPCODE,
  output [2:0] RS,
  output [2:0] RT,
  output [2:0] RD,
  output [7:0] Immediate
);

  ROM #(.addrWidth(10), .dataWidth(21), .misaligned("true")) rom_1 (
    .addr(Address), .data({OPCODE, RS, RT, RD[2], JUMP[9:8], Immediate}));

  assign JUMP[7:0] = Immediate;
  assign RD[1:0] = JUMP[9:8];
endmodule

module Data_Memory (
  input  [7:0] Address,
  input  WRITE,
  input  READ,
  input  Clk,
  input  [7:0] Write_data,
  output [7:0] Read_data
);

  RAM #(.asyncread("true"), .trigger("falling")) ram_1 (
    .addr(Address), .we(WRITE), .oe(READ), .clk(Clk), .din(Write_data), .dout(Read_data));
endmodule

module CPU (
);

  wire alu8_1_eq, Clk, control_1_branch, control_1_mux2, control_1_read, control_1_we, control_1_write;
  wire [1:0] and_1_out, bit_extender_2_out, control_1_mux1, control_1_pcmux;
  wire [2:0] control_1_alufunc, instruction_memory_1_rd, instruction_memory_1_rs, instruction_memory_1_rt;
  wire [3:0] instruction_memory_1_opcode;
  wire [7:0] alu8_1_result, data_memory_1_read_data, instruction_memory_1_immediate, multiplexer_2_out,
       multiplexer_3_out, reg_file_1_read_data1, reg_file_1_read_data2;
  wire [9:0] adder_1_out, adder_2_out, bit_extender_1_out, instruction_memory_1_jump, multiplexer_1_out,
       pc_1_addr_out;

  Clock clock_1 (.out(Clk));
  Multiplexer #(.select(2), .width(10)) multiplexer_1 (
    .in0(adder_2_out), .in1(adder_1_out), .in2(instruction_memory_1_jump), .out(multiplexer_1_out),
    .sel(and_1_out));  // open: in3
  assign bit_extender_1_out = {{2{instruction_memory_1_immediate[7]}}, instruction_memory_1_immediate};  // Bit_Extender bit_extender_1
  PC pc_1 (.addr_in(multiplexer_1_out), .Clk(Clk), .addr_out(pc_1_addr_out));
  Adder #(.width(10)) adder_1 (.a(bit_extender_1_out), .b(multiplexer_1_out), .out(adder_1_out));  // open: cin, cout
  Adder #(.width(10)) adder_2 (.a(10'h1), .b(pc_1_addr_out), .out(adder_2_out));  // open: cin, cout
  Instruction_Memory instruction_memory_1 (
    .Address(pc_1_addr_out), .JUMP(instruction_memory_1_jump), .OPCODE(instruction_memory_1_opcode),
    .RS(instruction_memory_1_rs), .RT(instruction_memory_1_rt), .RD(instruction_memory_1_rd),
    .Immediate(instruction_memory_1_immediate));
  CONTROL control_1 (
    .OPCODE(instruction_memory_1_opcode), .EQ(alu8_1_eq), .ALUfunc(control_1_alufunc), .Mux1(control_1_mux1),
    .Mux2(control_1_mux2), .WE(control_1_we), .Write(control_1_write), .Read(control_1_read),
    .PCmux(control_1_pcmux), .Branch(control_1_branch));
  Multiplexer #(.select(2), .width(8)) multiplexer_2 (
    .in0(alu8_1_result), .in1(data_memory_1_read_data), .in2(instruction_memory_1_immediate),
    .out(multiplexer_2_out), .sel(control_1_mux1));  // open: in3
  assign bit_extender_2_out = {{1{control_1_branch}}, control_1_branch};  // Bit_Extender bit_extender_2
  assign and_1_out = bit_extender_2_out & control_1_pcmux;  // AND_Gate and_1, 2 bits wide
  REG_FILE reg_file_1 (
    .WE(control_1_we), .RD(instruction_memory_1_rd), .Write_data(multiplexer_2_out), .Clk(Clk),
    .RS(instruction_memory_1_rs), .RT(instruction_memory_1_rt), .Read_data1(reg_file_1_read_data1),
    .Read_data2(reg_file_1_read_data2));
  Multiplexer #(.width(8)) multiplexer_3 (
    .in0(reg_file_1_read_data2), .in1(instruction_memory_1_immediate), .out(multiplexer_3_out),
    .sel(control_1_mux2));
  ALU8 alu8_1 (
    .X(reg_file_1_read_data1), .Y(multiplexer_3_out), .ALUfunc(control_1_alufunc), .EQ(alu8_1_eq),
    .RESULT(alu8_1_result));
  Data_Memory data_memory_1 (
    .Address(alu8_1_result), .WRITE(control_1_write), .READ(control_1_read), .Clk(Clk),
    .Write_data(reg_file_1_read_data2), .Read_data(data_memory_1_read_data));
endmodule

module PC (
  input  [9:0] addr_in,
  input  Clk,
  output [9:0] addr_out
);

  Register #(.trigger("falling"), .width(10)) register_1 (
    .D(addr_in), .en(1'b1), .clk(Clk), .Q(addr_out));  // open: clr
endmodule

module CONTROL (
  input  [3:0] OPCODE,
  input  EQ,
  output [2:0] ALUfunc,
  output [1:0] Mux1,
  output Mux2,
  output WE,
  output Write,
  output Read,
  output [1:0] PCmux,
  output Branch
);

  wire and_3_out, and_4_out, and_5_out, and_6_out, and_7_out, and_12_out, and_13_out, and_14_out, not_1_out,
       not_2_out, not_3_out, not_4_out, not_5_out, not_6_out, not_7_out, not_8_out, not_9_out, not_10_out,
       not_11_out, not_12_out, not_13_out, not_14_out, not_15_out, not_16_out, not_17_out, not_18_out,
       not_19_out;

  not not_1 (not_1_out, OPCODE[3]);
  not not_2 (not_2_out, OPCODE[1]);
  not not_3 (not_3_out, OPCODE[2]);
  not not_4 (not_4_out, OPCODE[2]);
  not not_5 (not_5_out, OPCODE[1]);
  not not_6 (not_6_out, OPCODE[0]);
  not not_7 (not_7_out, OPCODE[3]);
  not not_8 (not_8_out, OPCODE[2]);
  not not_9 (not_9_out, OPCODE[0]);
  not not_10 (not_10_out, OPCODE[2]);
  not not_11 (not_11_out, OPCODE[1]);
  not not_12 (not_12_out, OPCODE[2]);
  not not_13 (not_13_out, OPCODE[3]);
  not not_14 (not_14_out, OPCODE[2]);
  not not_15 (not_15_out, OPCODE[1]);
  not not_16 (not_16_out, OPCODE[3]);
  not not_17 (not_17_out, EQ);
  not not_18 (not_18_out, OPCODE[1]);
  not not_19 (not_19_out, OPCODE[0]);
  and and_1 (Mux1[1], not_1_out, OPCODE[1]);
  and and_2 (Mux1[0], not_2_out, OPCODE[0]);
  and and_3 (and_3_out, not_3_out, OPCODE[0]);
  and and_4 (and_4_out, not_4_out, OPCODE[1]);
  and and_5 (and_5_out, not_5_out, not_6_out);
  and and_6 (and_6_out, OPCODE[3], OPCODE[2]);
  and and_7 (and_7_out, not_7_out, not_8_out, OPCODE[0]);
  and and_8 (Write, OPCODE[1], not_9_out);
  and and_9 (Read, not_10_out, not_11_out, OPCODE[0]);
  and and_10 (PCmux[1], OPCODE[3], not_12_out, OPCODE[0]);
  and and_11 (PCmux[0], not_13_out, OPCODE[2], OPCODE[0]);
  and and_12 (and_12_out, OPCODE[3], not_14_out, OPCODE[0]);
  and and_13 (and_13_out, OPCODE[2], not_15_out, OPCODE[0], EQ);
  and and_14 (and_14_out, not_16_out, OPCODE[2], OPCODE[1], not_17_out);
  and and_15 (ALUfunc[2], OPCODE[0], OPCODE[2]);
  and and_16 (ALUfunc[1], OPCODE[3], not_18_out);
  and and_17 (ALUfunc[0], OPCODE[2], not_19_out);
  or or_1 (Mux2, and_3_out, and_4_out);
  or or_2 (WE, and_5_out, and_6_out, and_7_out);
  or or_3 (Branch, and_12_out, and_13_out, and_14_out);
endmodule
